# Fritzing sketch digital_alarm_clock (saved by Fritzing 1.0.8)
breadboards: 1

parts:
  Part1 = Arduino Uno (Rev3)
  LED1 = smd LED [color="Blue (430nm)" package="0805 [SMD]"]
  R1 = Resistor [tolerance=±5% resistance=150 package="0603 [SMD]"]
  S1 = Pushbutton [package="[THT]"]
  S2 = Pushbutton [package="[THT]"]
  S3 = Pushbutton [package="[THT]"]
  S4 = Pushbutton [package="[THT]"]
  LCD2004-I2C1 = LCD2004-I2C
  Mod1 = Passive Buzzer

nets:
  N1: Part1.A4/SDA, LCD2004-I2C1.SDA
  N2: Part1.A5/SCL, LCD2004-I2C1.SCL
  N3: Part1.D8, Mod1.NC
  GND: Part1.GND, Part1.D4, Part1.D5_PWM, Part1.D6_PWM, Part1.D7, LED1.cathode, S1.Pin_1, S1.Pin_2, S1.Pin_3, S1.Pin_4, S2.Pin_1, S2.Pin_2, S2.Pin_3, S2.Pin_4, S3.Pin_1, S3.Pin_2, S3.Pin_3, S3.Pin_4, S4.Pin_1, S4.Pin_2, S4.Pin_3, S4.Pin_4, LCD2004-I2C1.GND, Mod1.S
  N4: Part1.D3_PWM, R1.Pin_1
  5V: Part1.5V, LCD2004-I2C1.VCC, Mod1.-
  N5: LED1.anode, R1.Pin_0

custom parts:
  LCD2004-I2C: A standard character display with 4x20 characters. Comes in many colors with LCM2004 IIC attached.
